# Fritzing sketch IoTBox_Perfboard (saved by Fritzing 0.9.3b)
perfboards: 1

parts:
  J3 = Screw terminal - 2 pins [package=THT]
  S1 = SPST Switch [package=r_sw_th]
  LCD = Header 4 [package=jst-4-pth]
  Buzzer = Header 4 [package=jst-4-pth]
  Switch = Header 4 [package=jst-4-pth]
  J4 = Power Jack [package=power_jack_pth]
  J5 = Screw terminal - 2 pins [package=THT]
  L1 = Solenoid
  D1 = Diode [package=diode-1n4001]  # not connected
  Part1 = Photon  # not connected

nets:
  N1: J3.pin1, J4.GND
  N2: J3.pin2, S1.P
  N3: S1.O, J4.PWR
  N4: LCD.3, LCD.4
  N5: Buzzer.3, Buzzer.4
  N6: Switch.3, Switch.4
  N7: J5.pin1, L1.pin1
  N8: J5.pin2, L1.pin2
